# Fritzing sketch Fritzing Sketch (saved by Fritzing 0.9.3b)
breadboards: 1

parts:
  Part1 = Arduino Uno (Rev3)
  R1 = Resistor [tolerance=±5% resistance=10k package="1206 [SMD]"]
  R2 = Resistor [tolerance=±5% resistance=1k package="1206 [SMD]"]
  R3 = Resistor [tolerance=±5% resistance=1k package="1206 [SMD]"]
  R4 = Resistor [tolerance=±5% resistance=1k package="1206 [SMD]"]
  R5 = Resistor [tolerance=±5% resistance=1k package="1206 [SMD]"]
  R6 = Resistor [tolerance=±5% resistance=330 package="1206 [SMD]"]
  R7 = Resistor [tolerance=±5% resistance=330 package="1206 [SMD]"]
  R8 = Resistor [tolerance=±5% resistance=330 package="1206 [SMD]"]
  hc-sr1 = hc-sr04
  J1 = Piezo Speaker
  U1 = POT [package=pot_alpha_rv16af-20]
  LCD1 = LCD screen
  R9 = Resistor [tolerance=±5% resistance=330 package="0805 [SMD]"]

nets:
  N1: Part1.A0, R5.Pin_0
  N2: Part1.D9_PWM, hc-sr1.Trig
  N3: Part1.D10_PWM/SS, hc-sr1.Echo
  N4: Part1.D11_PWM/MOSI, J1.pin2
  N5: Part1.D12/MISO, LCD1.E
  N6: Part1.D13/SCK, LCD1.RS
  N7: Part1.D2, LCD1.DB7
  N8: Part1.D3_PWM, LCD1.DB6
  N9: Part1.D4, LCD1.DB5
  N10: Part1.D5_PWM, LCD1.DB4
  5V: Part1.5V, R1.Pin_0, hc-sr1.VCC, U1.A, LCD1.VDD, R9.Pin_1
  GND: Part1.GND, R8.Pin_1, hc-sr1.GND, J1.pin1, U1.E, LCD1.VSS, LCD1.R/W, LCD1.LED-
  N11: R1.Pin_1, R2.Pin_0, R5.Pin_1
  N12: R2.Pin_1, R3.Pin_0
  N13: R3.Pin_1, R4.Pin_0
  N14: R6.Pin_1, R7.Pin_0
  N15: R7.Pin_1, R8.Pin_0
  N16: U1.S, LCD1.V0
  N17: LCD1.LED+, R9.Pin_0

notes:
  D # 0 *
  C 9 8 7
  B 6 5 4
  A 3 2 1
  (Dibalik)
